// Logisim project circuit1c.circ as structural Verilog: 1 circuit, main circuit circuit1c
module circuit1c (
  input  A,
  input  B,
  input  C,
  output out1,
  output out2
);

  wire a_t, and_1_out, and_2_out, and_3_out, and_4_out, b_t, c_t;

  not not_1 (a_t, A);
  not not_2 (b_t, B);
  not not_3 (c_t, C);
  and and_1 (and_1_out, C, b_t, A);
  and and_2 (and_2_out, a_t, c_t);
  and and_3 (and_3_out, a_t, B);
  and and_4 (and_4_out, a_t, C);
  or or_1 (out1, and_1_out, and_2_out, and_3_out);
  or or_2 (out2, and_4_out, B);
endmodule
