// Logisim project vending.circ as structural Verilog: 2 circuits, main circuit main
module main (
  input  N,
  input  D,
  input  RESET,
  output DISPENSE,
  output DESPERATE,
  output DOH
);

  wire clock_1_out;

  Clock clock_1 (.out(clock_1_out));
  bodyCircuit bodycircuit_1 (
    .N(N), .D(D), .Reset(RESET), .clk(clock_1_out), .DISPENSE(DISPENSE), .DESPERATE(DESPERATE), .DOH(DOH));
endmodule

module bodyCircuit (
  input  N,
  input  D,
  input  Reset,
  input  clk,
  output DISPENSE,
  output DESPERATE,
  output DOH
);

  wire and_1_out, and_2_out, and_3_out, and_4_out, and_5_out, and_7_out, and_8_out, and_9_out, and_10_out,
       and_11_out, and_12_out, and_13_out, and_14_out, and_15_out, and_16_out, and_17_out, and_18_out,
       and_19_out, and_20_out, and_21_out, and_22_out, and_23_out, and_24_out, and_25_out, and_26_out,
       and_27_out, and_28_out, and_29_out, D2_out, D3_out, Nin1, Nin2, Nin3, NQ1, NQ2, NQ3, or_3_out,
       or_4_out, Q1, Q2, Q3;

  not not_1 (Nin1, N);
  not not_2 (Nin2, D);
  not not_3 (Nin3, Reset);
  and and_1 (and_1_out, Q1, Q2, NQ3);
  and and_2 (and_2_out, Q1, NQ2, Q3);
  and and_3 (and_3_out, Q1, NQ3);
  and and_4 (and_4_out, Q1, Q2, NQ3);
  and and_5 (and_5_out, Q1, NQ2, Q3);
  and and_6 (DOH, Q1, Q2, NQ3);
  or or_1 (DISPENSE, and_1_out, and_2_out, and_3_out);
  or or_2 (DESPERATE, and_4_out, and_5_out);
  and and_7 (and_7_out, NQ1, Q2, NQ3, Nin1, D);
  and and_8 (and_8_out, NQ1, Q2, Q3, N, Nin2);
  and and_9 (and_9_out, NQ1, Q2, Q3, Nin1, D);
  and and_10 (and_10_out, Q1, NQ2, NQ3, Nin3);
  and and_11 (and_11_out, Q1, NQ2, Q3, Nin3);
  and and_12 (and_12_out, Q1, Q2, NQ3, Nin3);
  and and_13 (and_13_out, NQ1, NQ2, Q3, Nin1, D);
  and and_14 (and_14_out, NQ1, Q2, NQ3, N, Nin2);
  and and_15 (and_15_out, Q1, NQ2, NQ3, Nin1, Nin2, Reset);
  and and_16 (and_16_out, Q1, NQ2, Q3, Nin1, Nin2, Reset);
  and and_17 (and_17_out, Q1, Q2, NQ3, Nin1, Nin2, Reset);
  or or_3 (or_3_out, and_13_out, and_14_out, and_7_out, and_8_out, and_9_out, and_10_out, and_11_out, and_12_out);
  or or_4 (or_4_out, and_15_out, and_16_out, and_17_out);
  D_Flip_Flop FF1 (.D(or_3_out), .clk(clk), .Q(Q1), .Qn(NQ1), .reset(or_4_out));  // open: preset
  and and_18 (and_18_out, Q1, Q2, NQ3, Nin3);
  and and_19 (and_19_out, NQ1, Q2, NQ3, Nin1, D);
  and and_20 (and_20_out, Q1, NQ2, Q3, Nin3);
  and and_21 (and_21_out, NQ1, NQ2, NQ3, Nin1, D);
  and and_22 (and_22_out, NQ1, NQ2, Q3, N, Nin2);
  and and_23 (and_23_out, NQ1, Q2, NQ3, Nin1, Nin2);
  and and_24 (and_24_out, NQ1, Q2, Q3, Nin1, D);
  and and_25 (and_25_out, NQ1, Q2, Q3, Nin1, Nin2);
  and and_26 (and_26_out, NQ1, NQ2, NQ3, N, Nin2);
  and and_27 (and_27_out, NQ1, NQ2, Q3, N, Nin2);
  and and_28 (and_28_out, NQ1, NQ2, Q3, Nin1, Nin2);
  and and_29 (and_29_out, NQ1, Q2, Q3, Nin1, Nin2);
  or D2 (D2_out, and_21_out, and_22_out, and_23_out, and_24_out, and_25_out, and_18_out);
  or D3 (D3_out, and_26_out, and_27_out, and_28_out, and_19_out, and_29_out, and_20_out);
  D_Flip_Flop FF2 (.D(D2_out), .clk(clk), .Q(Q2), .Qn(NQ2), .reset(or_4_out));  // open: preset
  D_Flip_Flop FF3 (.D(D3_out), .clk(clk), .Q(Q3), .Qn(NQ3), .reset(or_4_out));  // open: preset

  // Other names for the same wires on the sheet: in1 = N; in2 = D; in3 = Reset
endmodule
