// Logisim project cpu.circ as structural Verilog: 11 circuits, main circuit main
module main (
  input  reset
);

  wire alu_1_ofv, alu_1_smaller, alu_1_zero, ALUin2, and_1_out, and_2_out, BRne, BRnelt, clk, DMwe, jal, JP,
       JR, keyboard_1_avail, KeyIn, memory_latch_1_oe_latched, memory_latch_1_we_latched, multiplexer_8_out,
       not_1_out, not_2_out, not_4_out, not_5_out, or_1_out, OutKey, rdst, rijdecide_1_i, rijdecide_1_j, Rwd,
       Rwe, Shift;
  wire [2:0] ALUop, multiplexer_3_out, multiplexer_4_out, Rd, Rs, Rt, Shamt;
  wire [3:0] opcode;
  wire [5:0] bit_extender_5_out, demultiplexer_1_out0, Immed, multiplexer_5_out;
  wire [6:0] bit_extender_2_out;
  wire [7:0] keyboard_1_data;
  wire [11:0] Address, rom_1_data;
  wire [15:0] Add1_result, alu_1_out0, bit_extender_3_out, bit_extender_4_out, bitadder16_1_result, KeyVal,
       memory_latch_1_address_latched, memory_latch_1_data_in_latched, multiplexer_1_out, multiplexer_2_out,
       multiplexer_6_out, multiplexer_7_out, multiplexer_9_out, multiplexer_10_out, multiplexer_11_out, PC,
       ram_1_dout, registerfile_1_rtval, rsVAL;

  Clock u_clk (.out(clk));
  not not_1 (not_1_out, clk);
  Multiplexer #(.width(16)) multiplexer_1 (.in0(multiplexer_9_out), .in1(rsVAL), .out(multiplexer_1_out), .sel(JR));
  sixteenBitRegister u_PC (
    .reset(reset), .clk(not_1_out), .write_enabled(1'b1), .RegIn(multiplexer_1_out), .RegOut(PC));
  controlPath controlpath_1 (
    .opcode(opcode), .JP(JP), .JR(JR), .jal(jal), .KeyIn(KeyIn), .OutKey(OutKey), .Rwe(Rwe), .ALUin2(ALUin2),
    .rdst(rdst), .ALUop(ALUop), .Shift(Shift), .Rwd(Rwd), .DMwe(DMwe), .BRne(BRne), .BRnelt(BRnelt));
  ROM #(.addrWidth(16), .dataWidth(16)) rom_1 (.addr(PC), .data({opcode, rom_1_data}));
  BitAdder16 Add1 (.sub(1'b0), .in0(16'h1), .in1(PC), .result(Add1_result));  // open: ovf
  not not_2 (not_2_out, clk);
  Keyboard keyboard_1 (.clk(not_2_out), .re(KeyIn), .clr(reset), .avail(keyboard_1_avail), .data(keyboard_1_data[6:0]));
  Demultiplexer #(.width(12)) demultiplexer_1 (
    .out0({Rs, Rt, demultiplexer_1_out0}), .out1(Address), .in(rom_1_data), .sel(rijdecide_1_j));
  RIJDecide rijdecide_1 (.instruction({opcode, rom_1_data}), .I(rijdecide_1_i), .J(rijdecide_1_j));  // open: R
  Demultiplexer #(.width(6)) demultiplexer_2 (
    .out0({Rd, Shamt}), .out1(Immed), .in(demultiplexer_1_out0), .sel(rijdecide_1_i));
  not not_3 (keyboard_1_data[7], keyboard_1_avail);
  assign KeyVal = {{8{1'b0}}, keyboard_1_data};  // Bit_Extender bit_extender_1
  Multiplexer #(.width(16)) multiplexer_2 (
    .in0(multiplexer_11_out), .in1(Add1_result), .out(multiplexer_2_out), .sel(jal));
  Bit_Extender #(.in_width(16), .out_width(7)) bit_extender_2 (.in(rsVAL), .out(bit_extender_2_out));
  TTY #(.cols(80), .rows(13)) tty_1 (.data(bit_extender_2_out), .clk(clk), .we(OutKey), .clr(reset));
  Multiplexer #(.width(3)) multiplexer_3 (.in0(multiplexer_4_out), .in1(3'b111), .out(multiplexer_3_out), .sel(jal));
  Multiplexer #(.width(3)) multiplexer_4 (.in0(Rd), .in1(Rt), .out(multiplexer_4_out), .sel(rdst));
  RegisterFile registerfile_1 (
    .WE(Rwe), .reset(reset), .clk(clk), .rd(multiplexer_3_out), .rs(Rs), .rt(Rt),
    .WriteData(multiplexer_2_out), .rsVAL(rsVAL), .rtVAL(registerfile_1_rtval));
  assign bit_extender_3_out = {{4{1'b0}}, Address};  // Bit_Extender bit_extender_3
  assign bit_extender_4_out = {{10{multiplexer_5_out[5]}}, multiplexer_5_out};  // Bit_Extender bit_extender_4
  Multiplexer #(.width(6)) multiplexer_5 (.in0(Immed), .in1(bit_extender_5_out), .out(multiplexer_5_out), .sel(Shift));
  assign bit_extender_5_out = {{3{1'b0}}, Shamt};  // Bit_Extender bit_extender_5
  Multiplexer #(.width(16)) multiplexer_6 (
    .in0(registerfile_1_rtval), .in1(bit_extender_4_out), .out(multiplexer_6_out), .sel(ALUin2));
  ALU alu_1 (
    .OpType(ALUop), .in0(rsVAL), .in1(multiplexer_6_out), .ofv(alu_1_ofv), .out0(alu_1_out0),
    .Smaller(alu_1_smaller), .Zero(alu_1_zero));
  not not_4 (not_4_out, clk);
  and and_1 (and_1_out, BRne, not_5_out);
  not not_5 (not_5_out, alu_1_zero);
  and and_2 (and_2_out, BRnelt, alu_1_smaller);
  RAM #(.addrWidth(16), .dataWidth(16), .trigger("high")) ram_1 (
    .addr(memory_latch_1_address_latched), .we(memory_latch_1_we_latched), .oe(memory_latch_1_oe_latched),
    .din(memory_latch_1_data_in_latched), .dout(ram_1_dout));
  memory_latch memory_latch_1 (
    .WE(DMwe), .clk(not_4_out), .data_in(registerfile_1_rtval), .address(alu_1_out0),
    .address_latched(memory_latch_1_address_latched), .WE_latched(memory_latch_1_we_latched),
    .OE_latched(memory_latch_1_oe_latched), .data_in_latched(memory_latch_1_data_in_latched));
  Multiplexer #(.width(16)) multiplexer_7 (
    .in0(Add1_result), .in1(bitadder16_1_result), .out(multiplexer_7_out), .sel(multiplexer_8_out));
  BitAdder16 bitadder16_1 (
    .sub(1'b0), .in0(Add1_result), .in1(bit_extender_4_out), .result(bitadder16_1_result));  // open: ovf
  Multiplexer multiplexer_8 (.in0(and_1_out), .in1(or_1_out), .out(multiplexer_8_out), .sel(BRnelt));
  or or_1 (or_1_out, alu_1_zero, and_2_out);
  Multiplexer #(.width(16)) multiplexer_9 (
    .in0(multiplexer_7_out), .in1(bit_extender_3_out), .out(multiplexer_9_out), .sel(JP));
  Multiplexer #(.width(16)) multiplexer_10 (.in0(alu_1_out0), .in1(ram_1_dout), .out(multiplexer_10_out), .sel(Rwd));
  Multiplexer #(.width(16)) multiplexer_11 (
    .in0(multiplexer_10_out), .in1(KeyVal), .out(multiplexer_11_out), .sel(KeyIn));
endmodule

module RegisterFile (
  input  reset,
  input  clk,
  input  WE,
  input  [2:0] rd,
  input  [2:0] rs,
  input  [2:0] rt,
  input  [15:0] WriteData,
  output [15:0] rsVAL,
  output [15:0] rtVAL
);

  wire E0, E1, E2, E3, E4, E5, E6, E7, RE00, RE01, RE02, RE03, RE04, RE05, RE06, RE07, RE10, RE11, RE12,
       RE13, RE14, RE15, RE16, RE17, WE0, WE1, WE2, WE3, WE4, WE5, WE6, WE7;
  wire [15:0] out0, out1, out2, out3, out4, out5, out6, out7;

  Decoder #(.select(3)) decoder_1 (
    .out0(E0), .out1(E1), .out2(E2), .out3(E3), .out4(E4), .out5(E5), .out6(E6), .out7(E7), .sel(rd));  // open: en
  and and_1 (WE0, E0, WE);
  and and_2 (WE1, E1, WE);
  and and_3 (WE2, E2, WE);
  and and_4 (WE3, E3, WE);
  and and_5 (WE4, E4, WE);
  and and_6 (WE5, E5, WE);
  and and_7 (WE6, E6, WE);
  and and_8 (WE7, E7, WE);
  Decoder #(.select(3)) decoder_2 (
    .out0(RE00), .out1(RE01), .out2(RE02), .out3(RE03), .out4(RE04), .out5(RE05), .out6(RE06), .out7(RE07),
    .sel(rs));  // open: en
  Decoder #(.select(3)) decoder_3 (
    .out0(RE10), .out1(RE11), .out2(RE12), .out3(RE13), .out4(RE14), .out5(RE15), .out6(RE16), .out7(RE17),
    .sel(rt));  // open: en
  sixteenBitRegister sixteenbitregister_1 (
    .reset(reset), .clk(clk), .write_enabled(WE0), .RegIn(WriteData), .RegOut(out0));
  // Probe on out0
  sixteenBitRegister sixteenbitregister_2 (
    .reset(reset), .clk(clk), .write_enabled(WE1), .RegIn(WriteData), .RegOut(out1));
  // Probe on out1
  sixteenBitRegister sixteenbitregister_3 (
    .reset(reset), .clk(clk), .write_enabled(WE2), .RegIn(WriteData), .RegOut(out2));
  // Probe on out2
  sixteenBitRegister sixteenbitregister_4 (
    .reset(reset), .clk(clk), .write_enabled(WE3), .RegIn(WriteData), .RegOut(out3));
  // Probe on out3
  assign rsVAL = RE00 ? out0 : 16'bz;  // Controlled_Buffer controlled_buffer_1
  assign rsVAL = RE01 ? out1 : 16'bz;  // Controlled_Buffer controlled_buffer_2
  assign rsVAL = RE02 ? out2 : 16'bz;  // Controlled_Buffer controlled_buffer_3
  assign rsVAL = RE03 ? out3 : 16'bz;  // Controlled_Buffer controlled_buffer_4
  assign rsVAL = RE04 ? out4 : 16'bz;  // Controlled_Buffer controlled_buffer_5
  assign rsVAL = RE05 ? out5 : 16'bz;  // Controlled_Buffer controlled_buffer_6
  assign rsVAL = RE06 ? out6 : 16'bz;  // Controlled_Buffer controlled_buffer_7
  assign rsVAL = RE07 ? out7 : 16'bz;  // Controlled_Buffer controlled_buffer_8
  assign rtVAL = RE10 ? out0 : 16'bz;  // Controlled_Buffer controlled_buffer_9
  assign rtVAL = RE11 ? out1 : 16'bz;  // Controlled_Buffer controlled_buffer_10
  assign rtVAL = RE12 ? out2 : 16'bz;  // Controlled_Buffer controlled_buffer_11
  assign rtVAL = RE13 ? out3 : 16'bz;  // Controlled_Buffer controlled_buffer_12
  assign rtVAL = RE14 ? out4 : 16'bz;  // Controlled_Buffer controlled_buffer_13
  assign rtVAL = RE15 ? out5 : 16'bz;  // Controlled_Buffer controlled_buffer_14
  assign rtVAL = RE16 ? out6 : 16'bz;  // Controlled_Buffer controlled_buffer_15
  assign rtVAL = RE17 ? out7 : 16'bz;  // Controlled_Buffer controlled_buffer_16
  sixteenBitRegister sixteenbitregister_5 (
    .reset(reset), .clk(clk), .write_enabled(WE4), .RegIn(WriteData), .RegOut(out4));
  // Probe on out4
  sixteenBitRegister sixteenbitregister_6 (
    .reset(reset), .clk(clk), .write_enabled(WE5), .RegIn(WriteData), .RegOut(out5));
  // Probe on out5
  sixteenBitRegister sixteenbitregister_7 (
    .reset(reset), .clk(clk), .write_enabled(WE6), .RegIn(WriteData), .RegOut(out6));
  // Probe on out6
  sixteenBitRegister sixteenbitregister_8 (
    .reset(reset), .clk(clk), .write_enabled(WE7), .RegIn(WriteData), .RegOut(out7));
  // Probe on out7

  // Other names for the same wires on the sheet: output1[15:0] = rsVAL; output2[15:0] = rtVAL; rs0[2:0] = rs;
  //   rs1[2:0] = rt; WrData[15:0] = WriteData; WriteEnable = WE
endmodule

module sixteenBitRegister (
  input  reset,
  input  clk,
  input  write_enabled,
  input  [15:0] RegIn,
  output [15:0] RegOut
);

  wire and_1_out, and_2_out, and_3_out, and_4_out, and_5_out, and_6_out, and_7_out, and_8_out, and_9_out,
       and_10_out, and_11_out, and_12_out, and_13_out, and_14_out, and_15_out, and_16_out;

  D_Flip_Flop R0 (.D(RegIn[0]), .clk(and_1_out), .Q(RegOut[0]), .reset(reset));  // open: Qn, preset
  and and_1 (and_1_out, write_enabled, clk);
  D_Flip_Flop R1 (.D(RegIn[1]), .clk(and_2_out), .Q(RegOut[1]), .reset(reset));  // open: Qn, preset
  and and_2 (and_2_out, write_enabled, clk);
  D_Flip_Flop R2 (.D(RegIn[2]), .clk(and_3_out), .Q(RegOut[2]), .reset(reset));  // open: Qn, preset
  and and_3 (and_3_out, write_enabled, clk);
  D_Flip_Flop R3 (.D(RegIn[3]), .clk(and_4_out), .Q(RegOut[3]), .reset(reset));  // open: Qn, preset
  and and_4 (and_4_out, write_enabled, clk);
  D_Flip_Flop R4 (.D(RegIn[4]), .clk(and_5_out), .Q(RegOut[4]), .reset(reset));  // open: Qn, preset
  and and_5 (and_5_out, write_enabled, clk);
  D_Flip_Flop R5 (.D(RegIn[5]), .clk(and_6_out), .Q(RegOut[5]), .reset(reset));  // open: Qn, preset
  and and_6 (and_6_out, write_enabled, clk);
  D_Flip_Flop R6 (.D(RegIn[6]), .clk(and_7_out), .Q(RegOut[6]), .reset(reset));  // open: Qn, preset
  and and_7 (and_7_out, write_enabled, clk);
  D_Flip_Flop R7 (.D(RegIn[7]), .clk(and_8_out), .Q(RegOut[7]), .reset(reset));  // open: Qn, preset
  and and_8 (and_8_out, write_enabled, clk);
  D_Flip_Flop R8 (.D(RegIn[8]), .clk(and_9_out), .Q(RegOut[8]), .reset(reset));  // open: Qn, preset
  and and_9 (and_9_out, write_enabled, clk);
  D_Flip_Flop R9 (.D(RegIn[9]), .clk(and_10_out), .Q(RegOut[9]), .reset(reset));  // open: Qn, preset
  and and_10 (and_10_out, write_enabled, clk);
  D_Flip_Flop R10 (.D(RegIn[10]), .clk(and_11_out), .Q(RegOut[10]), .reset(reset));  // open: Qn, preset
  and and_11 (and_11_out, write_enabled, clk);
  D_Flip_Flop R11 (.D(RegIn[11]), .clk(and_12_out), .Q(RegOut[11]), .reset(reset));  // open: Qn, preset
  and and_12 (and_12_out, write_enabled, clk);
  D_Flip_Flop R12 (.D(RegIn[12]), .clk(and_13_out), .Q(RegOut[12]), .reset(reset));  // open: Qn, preset
  and and_13 (and_13_out, write_enabled, clk);
  D_Flip_Flop R13 (.D(RegIn[13]), .clk(and_14_out), .Q(RegOut[13]), .reset(reset));  // open: Qn, preset
  and and_14 (and_14_out, write_enabled, clk);
  D_Flip_Flop R14 (.D(RegIn[14]), .clk(and_15_out), .Q(RegOut[14]), .reset(reset));  // open: Qn, preset
  and and_15 (and_15_out, write_enabled, clk);
  D_Flip_Flop R15 (.D(RegIn[15]), .clk(and_16_out), .Q(RegOut[15]), .reset(reset));  // open: Qn, preset
  and and_16 (and_16_out, write_enabled, clk);

  // Other names for the same wires on the sheet: in0 = RegIn[0]; in1 = RegIn[1]; in2 = RegIn[2]; in3 = RegIn[3];
  //   in4 = RegIn[4]; in5 = RegIn[5]; in6 = RegIn[6]; in7 = RegIn[7]; in8 = RegIn[8]; in9 = RegIn[9];
  //   in10 = RegIn[10]; in11 = RegIn[11]; in12 = RegIn[12]; in13 = RegIn[13]; in14 = RegIn[14]; in15 = RegIn[15];
  //   out0 = RegOut[0]; out1 = RegOut[1]; out2 = RegOut[2]; out3 = RegOut[3]; out4 = RegOut[4]; out5 = RegOut[5];
  //   out6 = RegOut[6]; out7 = RegOut[7]; out8 = RegOut[8]; out9 = RegOut[9]; out10 = RegOut[10]; out11 = RegOut[11];
  //   out12 = RegOut[12]; out13 = RegOut[13]; out14 = RegOut[14]; out15 = RegOut[15]; WE = write_enabled
endmodule

module ALU (
  input  [15:0] in0,
  input  [15:0] in1,
  input  [2:0] OpType,
  output ofv,
  output [15:0] out0,
  output Zero,
  output Smaller
);

  wire bitadder16_1_ovf, bitadder16_2_ovf, not_2_out, not_3_out, not_4_out, not_5_out, not_6_out, not_7_out,
       not_8_out, not_9_out, not_10_out, not_11_out, not_12_out, not_13_out, not_14_out, not_15_out,
       not_16_out, not_17_out;
  wire [15:0] and_1_out, bitadder16_1_result, bitadder16_2_result, bitadder16_3_result, leftshift_1_out0,
       not_1_out, rightshift_1_out0, xor_1_out;

  assign not_1_out = ~in0;  // NOT_Gate not_1, 16 bits wide
  BitAdder16 bitadder16_1 (.sub(1'b0), .in0(in0), .in1(in1), .result(bitadder16_1_result), .ovf(bitadder16_1_ovf));
  BitAdder16 bitadder16_2 (.sub(1'b1), .in0(in0), .in1(in1), .result(bitadder16_2_result), .ovf(bitadder16_2_ovf));
  LeftShift leftshift_1 (.in0(in0), .LeftShift(in1), .out0(leftshift_1_out0));
  RightShift rightshift_1 (.in0(in0), .RightShift(in1), .out0(rightshift_1_out0));
  assign and_1_out = in0 & in1;  // AND_Gate and_1, 16 bits wide
  BitAdder16 bitadder16_3 (.sub(1'b1), .in0(in0), .in1(in1), .result(bitadder16_3_result));  // open: ovf
  assign xor_1_out = bitadder16_3_result ^ {16{1'b0}};  // XOR_Gate xor_1, 16 bits wide
  Multiplexer #(.select(3)) multiplexer_1 (
    .in0(bitadder16_1_ovf), .in1(bitadder16_2_ovf), .out(ofv), .sel(OpType));  // open: in2, in3, in4, in5, in6, in7
  Multiplexer #(.select(3), .width(16)) multiplexer_2 (
    .in0(bitadder16_1_result), .in1(bitadder16_2_result), .in2(leftshift_1_out0), .in3(rightshift_1_out0),
    .in4(and_1_out), .in5(not_1_out), .out(out0), .sel(OpType));  // open: in6, in7
  not not_2 (not_2_out, xor_1_out[0]);
  not not_3 (not_3_out, xor_1_out[1]);
  not not_4 (not_4_out, xor_1_out[2]);
  not not_5 (not_5_out, xor_1_out[3]);
  not not_6 (not_6_out, xor_1_out[4]);
  not not_7 (not_7_out, xor_1_out[5]);
  not not_8 (not_8_out, xor_1_out[6]);
  not not_9 (not_9_out, xor_1_out[7]);
  not not_10 (not_10_out, xor_1_out[8]);
  not not_11 (not_11_out, xor_1_out[9]);
  not not_12 (not_12_out, xor_1_out[10]);
  not not_13 (not_13_out, xor_1_out[11]);
  not not_14 (not_14_out, xor_1_out[12]);
  not not_15 (not_15_out, xor_1_out[13]);
  not not_16 (not_16_out, xor_1_out[14]);
  not not_17 (not_17_out, xor_1_out[15]);
  and and_2 (Smaller, bitadder16_3_result[15], 1'b1);
  and and_3 (Zero, 1'b1, not_2_out, not_3_out, not_4_out, not_5_out, not_6_out, not_7_out, not_8_out, not_9_out, not_10_out, not_11_out, not_12_out, not_13_out, not_14_out, not_15_out, not_16_out, not_17_out);
endmodule

module BitAdder16 (
  input  sub,
  input  [15:0] in0,
  input  [15:0] in1,
  output [15:0] result,
  output ovf
);

  wire B1, B2, B3, B4, B5, B6, B7, B8, B9, B10, B11, B12, B13, B14, B15, B16, bitadder1_16_cout, Cout1,
       Cout2, Cout3, Cout4, Cout5, Cout6, Cout7, Cout8, Cout9, Cout10, Cout11, Cout12, Cout13, Cout14, Cout15;

  xor xor_1 (B1, sub, in1[0]);
  xor xor_2 (B2, sub, in1[1]);
  xor xor_3 (B3, sub, in1[2]);
  xor xor_4 (B4, sub, in1[3]);
  xor xor_5 (B5, sub, in1[4]);
  xor xor_6 (B6, sub, in1[5]);
  xor xor_7 (B7, sub, in1[6]);
  xor xor_8 (B8, sub, in1[7]);
  xor xor_9 (B9, sub, in1[8]);
  xor xor_10 (B10, sub, in1[9]);
  xor xor_11 (B11, sub, in1[10]);
  xor xor_12 (B12, sub, in1[11]);
  xor xor_13 (B13, sub, in1[12]);
  xor xor_14 (B14, sub, in1[13]);
  xor xor_15 (B15, sub, in1[14]);
  xor xor_16 (B16, sub, in1[15]);
  BitAdder1 bitadder1_1 (.A(in0[0]), .B(B1), .Cin(sub), .result(result[0]), .Cout(Cout1));
  BitAdder1 bitadder1_2 (.A(in0[1]), .B(B2), .Cin(Cout1), .result(result[1]), .Cout(Cout2));
  BitAdder1 bitadder1_3 (.A(in0[2]), .B(B3), .Cin(Cout2), .result(result[2]), .Cout(Cout3));
  BitAdder1 bitadder1_4 (.A(in0[3]), .B(B4), .Cin(Cout3), .result(result[3]), .Cout(Cout4));
  BitAdder1 bitadder1_5 (.A(in0[4]), .B(B5), .Cin(Cout4), .result(result[4]), .Cout(Cout5));
  BitAdder1 bitadder1_6 (.A(in0[5]), .B(B6), .Cin(Cout5), .result(result[5]), .Cout(Cout6));
  BitAdder1 bitadder1_7 (.A(in0[6]), .B(B7), .Cin(Cout6), .result(result[6]), .Cout(Cout7));
  BitAdder1 bitadder1_8 (.A(in0[7]), .B(B8), .Cin(Cout7), .result(result[7]), .Cout(Cout8));
  BitAdder1 bitadder1_9 (.A(in0[8]), .B(B9), .Cin(Cout8), .result(result[8]), .Cout(Cout9));
  BitAdder1 bitadder1_10 (.A(in0[9]), .B(B10), .Cin(Cout9), .result(result[9]), .Cout(Cout10));
  BitAdder1 bitadder1_11 (.A(in0[10]), .B(B11), .Cin(Cout10), .result(result[10]), .Cout(Cout11));
  BitAdder1 bitadder1_12 (.A(in0[11]), .B(B12), .Cin(Cout11), .result(result[11]), .Cout(Cout12));
  BitAdder1 bitadder1_13 (.A(in0[12]), .B(B13), .Cin(Cout12), .result(result[12]), .Cout(Cout13));
  BitAdder1 bitadder1_14 (.A(in0[13]), .B(B14), .Cin(Cout13), .result(result[13]), .Cout(Cout14));
  BitAdder1 bitadder1_15 (.A(in0[14]), .B(B15), .Cin(Cout14), .result(result[14]), .Cout(Cout15));
  BitAdder1 bitadder1_16 (.A(in0[15]), .B(B16), .Cin(Cout15), .result(result[15]), .Cout(bitadder1_16_cout));
  xor xor_17 (ovf, bitadder1_16_cout, Cout15);

  // Other names for the same wires on the sheet: A1 = in0[0]; A2 = in0[1]; A3 = in0[2]; A4 = in0[3]; A5 = in0[4];
  //   A6 = in0[5]; A7 = in0[6]; A8 = in0[7]; A9 = in0[8]; A10 = in0[9]; A11 = in0[10]; A12 = in0[11]; A13 = in0[12];
  //   A14 = in0[13]; A15 = in0[14]; A16 = in0[15]; b1_t = in1[0]; b2_t = in1[1]; b3_t = in1[2]; b4_t = in1[3];
  //   b5_t = in1[4]; b6_t = in1[5]; b7_t = in1[6]; b8_t = in1[7]; b9_t = in1[8]; b10_t = in1[9]; b11_t = in1[10];
  //   b12_t = in1[11]; b13_t = in1[12]; b14_t = in1[13]; b15_t = in1[14]; b16_t = in1[15]
endmodule

module BitAdder1 (
  input  A,
  input  B,
  input  Cin,
  output result,
  output Cout
);

  wire and_1_out, and_2_out, xor_1_out;

  xor xor_1 (xor_1_out, A, B);
  and and_1 (and_1_out, A, B);
  and and_2 (and_2_out, xor_1_out, Cin);
  xor xor_2 (result, Cin, xor_1_out);
  or or_1 (Cout, and_2_out, and_1_out);

  // Other names for the same wires on the sheet: C = Cin
endmodule

module LeftShift (
  input  [15:0] in0,
  input  [15:0] LeftShift,
  output [15:0] out0
);

  wire FourShift, multiplexer_1_out, multiplexer_2_out, multiplexer_3_out, multiplexer_4_out,
       multiplexer_5_out, multiplexer_6_out, multiplexer_7_out, multiplexer_8_out, multiplexer_9_out,
       multiplexer_10_out, multiplexer_11_out, multiplexer_12_out, multiplexer_13_out, multiplexer_14_out,
       multiplexer_15_out, multiplexer_16_out, multiplexer_17_out, multiplexer_18_out, multiplexer_19_out,
       multiplexer_20_out, multiplexer_21_out, multiplexer_22_out, multiplexer_23_out, multiplexer_24_out,
       multiplexer_25_out, multiplexer_26_out, multiplexer_27_out, multiplexer_28_out, multiplexer_29_out,
       multiplexer_30_out, multiplexer_31_out, multiplexer_32_out, OneShift, TwoShift;

  Bit_Extender #(.in_width(16), .out_width(3)) bit_extender_1 (.in(LeftShift), .out({FourShift, TwoShift, OneShift}));
  Multiplexer multiplexer_1 (.in0(in0[15]), .in1(in0[11]), .out(multiplexer_1_out), .sel(FourShift));
  Multiplexer multiplexer_2 (.in0(in0[14]), .in1(in0[10]), .out(multiplexer_2_out), .sel(FourShift));
  Multiplexer multiplexer_3 (.in0(in0[13]), .in1(in0[9]), .out(multiplexer_3_out), .sel(FourShift));
  Multiplexer multiplexer_4 (.in0(in0[12]), .in1(in0[8]), .out(multiplexer_4_out), .sel(FourShift));
  Multiplexer multiplexer_5 (.in0(in0[11]), .in1(in0[7]), .out(multiplexer_5_out), .sel(FourShift));
  Multiplexer multiplexer_6 (.in0(in0[10]), .in1(in0[6]), .out(multiplexer_6_out), .sel(FourShift));
  Multiplexer multiplexer_7 (.in0(in0[9]), .in1(in0[5]), .out(multiplexer_7_out), .sel(FourShift));
  Multiplexer multiplexer_8 (.in0(in0[8]), .in1(in0[4]), .out(multiplexer_8_out), .sel(FourShift));
  Multiplexer multiplexer_9 (.in0(in0[7]), .in1(in0[3]), .out(multiplexer_9_out), .sel(FourShift));
  Multiplexer multiplexer_10 (.in0(in0[6]), .in1(in0[2]), .out(multiplexer_10_out), .sel(FourShift));
  Multiplexer multiplexer_11 (.in0(in0[5]), .in1(in0[1]), .out(multiplexer_11_out), .sel(FourShift));
  Multiplexer multiplexer_12 (.in0(in0[4]), .in1(in0[0]), .out(multiplexer_12_out), .sel(FourShift));
  Multiplexer multiplexer_13 (.in0(in0[3]), .in1(1'b0), .out(multiplexer_13_out), .sel(FourShift));
  Multiplexer multiplexer_14 (.in0(in0[2]), .in1(1'b0), .out(multiplexer_14_out), .sel(FourShift));
  Multiplexer multiplexer_15 (.in0(in0[1]), .in1(1'b0), .out(multiplexer_15_out), .sel(FourShift));
  Multiplexer multiplexer_16 (.in0(in0[0]), .in1(1'b0), .out(multiplexer_16_out), .sel(FourShift));
  Multiplexer multiplexer_17 (
    .in0(multiplexer_1_out), .in1(multiplexer_3_out), .out(multiplexer_17_out), .sel(TwoShift));
  Multiplexer multiplexer_18 (
    .in0(multiplexer_2_out), .in1(multiplexer_4_out), .out(multiplexer_18_out), .sel(TwoShift));
  Multiplexer multiplexer_19 (
    .in0(multiplexer_3_out), .in1(multiplexer_5_out), .out(multiplexer_19_out), .sel(TwoShift));
  Multiplexer multiplexer_20 (
    .in0(multiplexer_4_out), .in1(multiplexer_6_out), .out(multiplexer_20_out), .sel(TwoShift));
  Multiplexer multiplexer_21 (
    .in0(multiplexer_5_out), .in1(multiplexer_7_out), .out(multiplexer_21_out), .sel(TwoShift));
  Multiplexer multiplexer_22 (
    .in0(multiplexer_6_out), .in1(multiplexer_8_out), .out(multiplexer_22_out), .sel(TwoShift));
  Multiplexer multiplexer_23 (
    .in0(multiplexer_7_out), .in1(multiplexer_9_out), .out(multiplexer_23_out), .sel(TwoShift));
  Multiplexer multiplexer_24 (
    .in0(multiplexer_8_out), .in1(multiplexer_10_out), .out(multiplexer_24_out), .sel(TwoShift));
  Multiplexer multiplexer_25 (
    .in0(multiplexer_9_out), .in1(multiplexer_11_out), .out(multiplexer_25_out), .sel(TwoShift));
  Multiplexer multiplexer_26 (
    .in0(multiplexer_10_out), .in1(multiplexer_12_out), .out(multiplexer_26_out), .sel(TwoShift));
  Multiplexer multiplexer_27 (
    .in0(multiplexer_11_out), .in1(multiplexer_13_out), .out(multiplexer_27_out), .sel(TwoShift));
  Multiplexer multiplexer_28 (
    .in0(multiplexer_12_out), .in1(multiplexer_14_out), .out(multiplexer_28_out), .sel(TwoShift));
  Multiplexer multiplexer_29 (
    .in0(multiplexer_13_out), .in1(multiplexer_15_out), .out(multiplexer_29_out), .sel(TwoShift));
  Multiplexer multiplexer_30 (
    .in0(multiplexer_14_out), .in1(multiplexer_16_out), .out(multiplexer_30_out), .sel(TwoShift));
  Multiplexer multiplexer_31 (.in0(multiplexer_15_out), .in1(1'b0), .out(multiplexer_31_out), .sel(TwoShift));
  Multiplexer multiplexer_32 (.in0(multiplexer_16_out), .in1(1'b0), .out(multiplexer_32_out), .sel(TwoShift));
  Multiplexer multiplexer_33 (.in0(multiplexer_17_out), .in1(multiplexer_18_out), .out(out0[15]), .sel(OneShift));
  Multiplexer multiplexer_34 (.in0(multiplexer_18_out), .in1(multiplexer_19_out), .out(out0[14]), .sel(OneShift));
  Multiplexer multiplexer_35 (.in0(multiplexer_19_out), .in1(multiplexer_20_out), .out(out0[13]), .sel(OneShift));
  Multiplexer multiplexer_36 (.in0(multiplexer_20_out), .in1(multiplexer_21_out), .out(out0[12]), .sel(OneShift));
  Multiplexer multiplexer_37 (.in0(multiplexer_21_out), .in1(multiplexer_22_out), .out(out0[11]), .sel(OneShift));
  Multiplexer multiplexer_38 (.in0(multiplexer_22_out), .in1(multiplexer_23_out), .out(out0[10]), .sel(OneShift));
  Multiplexer multiplexer_39 (.in0(multiplexer_23_out), .in1(multiplexer_24_out), .out(out0[9]), .sel(OneShift));
  Multiplexer multiplexer_40 (.in0(multiplexer_24_out), .in1(multiplexer_25_out), .out(out0[8]), .sel(OneShift));
  Multiplexer multiplexer_41 (.in0(multiplexer_25_out), .in1(multiplexer_26_out), .out(out0[7]), .sel(OneShift));
  Multiplexer multiplexer_42 (.in0(multiplexer_26_out), .in1(multiplexer_27_out), .out(out0[6]), .sel(OneShift));
  Multiplexer multiplexer_43 (.in0(multiplexer_27_out), .in1(multiplexer_28_out), .out(out0[5]), .sel(OneShift));
  Multiplexer multiplexer_44 (.in0(multiplexer_28_out), .in1(multiplexer_29_out), .out(out0[4]), .sel(OneShift));
  Multiplexer multiplexer_45 (.in0(multiplexer_29_out), .in1(multiplexer_30_out), .out(out0[3]), .sel(OneShift));
  Multiplexer multiplexer_46 (.in0(multiplexer_30_out), .in1(multiplexer_31_out), .out(out0[2]), .sel(OneShift));
  Multiplexer multiplexer_47 (.in0(multiplexer_31_out), .in1(multiplexer_32_out), .out(out0[1]), .sel(OneShift));
  Multiplexer multiplexer_48 (.in0(multiplexer_32_out), .in1(1'b0), .out(out0[0]), .sel(OneShift));

  // Other names for the same wires on the sheet: in0_t = in0[0]; in1 = in0[1]; in2 = in0[2]; in3 = in0[3];
  //   in4 = in0[4]; in5 = in0[5]; in6 = in0[6]; in7 = in0[7]; in8 = in0[8]; in9 = in0[9]; in10 = in0[10];
  //   in11 = in0[11]; in12 = in0[12]; in13 = in0[13]; in14 = in0[14]; in15 = in0[15]; out0_t = out0[0];
  //   out1 = out0[1]; out2 = out0[2]; out3 = out0[3]; out4 = out0[4]; out5 = out0[5]; out6 = out0[6]; out7 = out0[7];
  //   out8 = out0[8]; out9 = out0[9]; out10 = out0[10]; out11 = out0[11]; out12 = out0[12]; out13 = out0[13];
  //   out14 = out0[14]; out15 = out0[15]
endmodule

module RightShift (
  input  [15:0] in0,
  input  [15:0] RightShift,
  output [15:0] out0
);

  wire FourShift, multiplexer_1_out, multiplexer_2_out, multiplexer_3_out, multiplexer_4_out,
       multiplexer_5_out, multiplexer_6_out, multiplexer_7_out, multiplexer_8_out, multiplexer_9_out,
       multiplexer_10_out, multiplexer_11_out, multiplexer_12_out, multiplexer_13_out, multiplexer_14_out,
       multiplexer_15_out, multiplexer_16_out, multiplexer_17_out, multiplexer_18_out, multiplexer_19_out,
       multiplexer_20_out, multiplexer_21_out, multiplexer_22_out, multiplexer_23_out, multiplexer_24_out,
       multiplexer_25_out, multiplexer_26_out, multiplexer_27_out, multiplexer_28_out, multiplexer_29_out,
       multiplexer_30_out, multiplexer_31_out, multiplexer_32_out, OneShift, TwoShift;

  Bit_Extender #(.in_width(16), .out_width(3)) bit_extender_1 (.in(RightShift), .out({FourShift, TwoShift, OneShift}));
  Multiplexer multiplexer_1 (.in0(in0[0]), .in1(in0[4]), .out(multiplexer_1_out), .sel(FourShift));
  Multiplexer multiplexer_2 (.in0(in0[1]), .in1(in0[5]), .out(multiplexer_2_out), .sel(FourShift));
  Multiplexer multiplexer_3 (.in0(in0[2]), .in1(in0[6]), .out(multiplexer_3_out), .sel(FourShift));
  Multiplexer multiplexer_4 (.in0(in0[3]), .in1(in0[7]), .out(multiplexer_4_out), .sel(FourShift));
  Multiplexer multiplexer_5 (.in0(in0[4]), .in1(in0[8]), .out(multiplexer_5_out), .sel(FourShift));
  Multiplexer multiplexer_6 (.in0(in0[5]), .in1(in0[9]), .out(multiplexer_6_out), .sel(FourShift));
  Multiplexer multiplexer_7 (.in0(in0[6]), .in1(in0[10]), .out(multiplexer_7_out), .sel(FourShift));
  Multiplexer multiplexer_8 (.in0(in0[7]), .in1(in0[11]), .out(multiplexer_8_out), .sel(FourShift));
  Multiplexer multiplexer_9 (.in0(in0[8]), .in1(in0[12]), .out(multiplexer_9_out), .sel(FourShift));
  Multiplexer multiplexer_10 (.in0(in0[9]), .in1(in0[13]), .out(multiplexer_10_out), .sel(FourShift));
  Multiplexer multiplexer_11 (.in0(in0[10]), .in1(in0[14]), .out(multiplexer_11_out), .sel(FourShift));
  Multiplexer multiplexer_12 (.in0(in0[11]), .in1(in0[15]), .out(multiplexer_12_out), .sel(FourShift));
  Multiplexer multiplexer_13 (.in0(in0[12]), .in1(1'b0), .out(multiplexer_13_out), .sel(FourShift));
  Multiplexer multiplexer_14 (.in0(in0[13]), .in1(1'b0), .out(multiplexer_14_out), .sel(FourShift));
  Multiplexer multiplexer_15 (.in0(in0[14]), .in1(1'b0), .out(multiplexer_15_out), .sel(FourShift));
  Multiplexer multiplexer_16 (.in0(in0[15]), .in1(1'b0), .out(multiplexer_16_out), .sel(FourShift));
  Multiplexer multiplexer_17 (
    .in0(multiplexer_1_out), .in1(multiplexer_3_out), .out(multiplexer_17_out), .sel(TwoShift));
  Multiplexer multiplexer_18 (
    .in0(multiplexer_2_out), .in1(multiplexer_4_out), .out(multiplexer_18_out), .sel(TwoShift));
  Multiplexer multiplexer_19 (
    .in0(multiplexer_3_out), .in1(multiplexer_5_out), .out(multiplexer_19_out), .sel(TwoShift));
  Multiplexer multiplexer_20 (
    .in0(multiplexer_4_out), .in1(multiplexer_6_out), .out(multiplexer_20_out), .sel(TwoShift));
  Multiplexer multiplexer_21 (
    .in0(multiplexer_5_out), .in1(multiplexer_7_out), .out(multiplexer_21_out), .sel(TwoShift));
  Multiplexer multiplexer_22 (
    .in0(multiplexer_6_out), .in1(multiplexer_8_out), .out(multiplexer_22_out), .sel(TwoShift));
  Multiplexer multiplexer_23 (
    .in0(multiplexer_7_out), .in1(multiplexer_9_out), .out(multiplexer_23_out), .sel(TwoShift));
  Multiplexer multiplexer_24 (
    .in0(multiplexer_8_out), .in1(multiplexer_10_out), .out(multiplexer_24_out), .sel(TwoShift));
  Multiplexer multiplexer_25 (
    .in0(multiplexer_9_out), .in1(multiplexer_11_out), .out(multiplexer_25_out), .sel(TwoShift));
  Multiplexer multiplexer_26 (
    .in0(multiplexer_10_out), .in1(multiplexer_12_out), .out(multiplexer_26_out), .sel(TwoShift));
  Multiplexer multiplexer_27 (
    .in0(multiplexer_11_out), .in1(multiplexer_13_out), .out(multiplexer_27_out), .sel(TwoShift));
  Multiplexer multiplexer_28 (
    .in0(multiplexer_12_out), .in1(multiplexer_14_out), .out(multiplexer_28_out), .sel(TwoShift));
  Multiplexer multiplexer_29 (
    .in0(multiplexer_13_out), .in1(multiplexer_15_out), .out(multiplexer_29_out), .sel(TwoShift));
  Multiplexer multiplexer_30 (
    .in0(multiplexer_14_out), .in1(multiplexer_16_out), .out(multiplexer_30_out), .sel(TwoShift));
  Multiplexer multiplexer_31 (.in0(multiplexer_15_out), .in1(1'b0), .out(multiplexer_31_out), .sel(TwoShift));
  Multiplexer multiplexer_32 (.in0(multiplexer_16_out), .in1(1'b0), .out(multiplexer_32_out), .sel(TwoShift));
  Multiplexer multiplexer_33 (.in0(multiplexer_17_out), .in1(multiplexer_18_out), .out(out0[0]), .sel(OneShift));
  Multiplexer multiplexer_34 (.in0(multiplexer_18_out), .in1(multiplexer_19_out), .out(out0[1]), .sel(OneShift));
  Multiplexer multiplexer_35 (.in0(multiplexer_19_out), .in1(multiplexer_20_out), .out(out0[2]), .sel(OneShift));
  Multiplexer multiplexer_36 (.in0(multiplexer_20_out), .in1(multiplexer_21_out), .out(out0[3]), .sel(OneShift));
  Multiplexer multiplexer_37 (.in0(multiplexer_21_out), .in1(multiplexer_22_out), .out(out0[4]), .sel(OneShift));
  Multiplexer multiplexer_38 (.in0(multiplexer_22_out), .in1(multiplexer_23_out), .out(out0[5]), .sel(OneShift));
  Multiplexer multiplexer_39 (.in0(multiplexer_23_out), .in1(multiplexer_24_out), .out(out0[6]), .sel(OneShift));
  Multiplexer multiplexer_40 (.in0(multiplexer_24_out), .in1(multiplexer_25_out), .out(out0[7]), .sel(OneShift));
  Multiplexer multiplexer_41 (.in0(multiplexer_25_out), .in1(multiplexer_26_out), .out(out0[8]), .sel(OneShift));
  Multiplexer multiplexer_42 (.in0(multiplexer_26_out), .in1(multiplexer_27_out), .out(out0[9]), .sel(OneShift));
  Multiplexer multiplexer_43 (.in0(multiplexer_27_out), .in1(multiplexer_28_out), .out(out0[10]), .sel(OneShift));
  Multiplexer multiplexer_44 (.in0(multiplexer_28_out), .in1(multiplexer_29_out), .out(out0[11]), .sel(OneShift));
  Multiplexer multiplexer_45 (.in0(multiplexer_29_out), .in1(multiplexer_30_out), .out(out0[12]), .sel(OneShift));
  Multiplexer multiplexer_46 (.in0(multiplexer_30_out), .in1(multiplexer_31_out), .out(out0[13]), .sel(OneShift));
  Multiplexer multiplexer_47 (.in0(multiplexer_31_out), .in1(multiplexer_32_out), .out(out0[14]), .sel(OneShift));
  Multiplexer multiplexer_48 (.in0(multiplexer_32_out), .in1(1'b0), .out(out0[15]), .sel(OneShift));

  // Other names for the same wires on the sheet: in0_t = in0[0]; in1 = in0[1]; in2 = in0[2]; in3 = in0[3];
  //   in4 = in0[4]; in5 = in0[5]; in6 = in0[6]; in7 = in0[7]; in8 = in0[8]; in9 = in0[9]; in10 = in0[10];
  //   in11 = in0[11]; in12 = in0[12]; in13 = in0[13]; in14 = in0[14]; in15 = in0[15]; out0_t = out0[0];
  //   out1 = out0[1]; out2 = out0[2]; out3 = out0[3]; out4 = out0[4]; out5 = out0[5]; out6 = out0[6]; out7 = out0[7];
  //   out8 = out0[8]; out9 = out0[9]; out10 = out0[10]; out11 = out0[11]; out12 = out0[12]; out13 = out0[13];
  //   out14 = out0[14]; out15 = out0[15]
endmodule

module controlPath (
  input  [3:0] opcode,
  output Rwe,
  output ALUin2,
  output rdst,
  output Shift,
  output Rwd,
  output DMwe,
  output BRne,
  output BRnelt,
  output JP,
  output JR,
  output jal,
  output KeyIn,
  output OutKey,
  output [2:0] ALUop
);

  wire decoder_1_out0, decoder_1_out1, decoder_1_out2, decoder_1_out3, decoder_1_out4, decoder_1_out5,
       decoder_1_out6, decoder_1_out11;

  Decoder #(.select(4)) decoder_1 (
    .out0(decoder_1_out0), .out1(decoder_1_out1), .out2(decoder_1_out2), .out3(decoder_1_out3),
    .out4(decoder_1_out4), .out5(decoder_1_out5), .out6(decoder_1_out6), .out7(Rwd), .out8(DMwe),
    .out9(BRne), .out10(BRnelt), .out11(decoder_1_out11), .out12(JR), .out13(jal), .out14(KeyIn),
    .out15(OutKey), .sel(opcode));  // open: en
  or or_1 (Rwe, decoder_1_out0, decoder_1_out1, decoder_1_out2, decoder_1_out3, decoder_1_out4, decoder_1_out5, decoder_1_out6, Rwd, jal, KeyIn);
  or or_2 (ALUin2, decoder_1_out1, decoder_1_out3, decoder_1_out4, Rwd, DMwe);
  or or_3 (rdst, decoder_1_out1, Rwd, DMwe, KeyIn);
  or or_4 (ALUop[2], decoder_1_out5, decoder_1_out6);
  or or_5 (ALUop[1], decoder_1_out3, decoder_1_out4);
  or or_6 (Shift, decoder_1_out3, decoder_1_out4);
  or or_7 (ALUop[0], decoder_1_out2, decoder_1_out4, decoder_1_out6, BRne, BRnelt);
  or or_8 (JP, decoder_1_out11, jal);
endmodule

module memory_latch (
  input  [15:0] address,
  input  WE,
  input  clk,
  input  [15:0] data_in,
  output [15:0] address_latched,
  output WE_latched,
  output OE_latched,
  output [15:0] data_in_latched
);

  wire DMwe_latch_q;
  wire [15:0] addr_latch_q;

  Register #(.trigger("falling"), .width(16)) addr_latch (
    .D(address), .en(WE), .clk(clk), .Q(addr_latch_q));  // open: clr
  D_Flip_Flop #(.trigger("falling")) DMwe_latch (.D(WE), .clk(clk), .Q(DMwe_latch_q));  // open: Qn, preset, reset
  Register #(.trigger("falling"), .width(16)) data_to_be_written (
    .D(data_in), .en(WE), .clk(clk), .Q(data_in_latched));  // open: clr
  Multiplexer #(.width(16)) multiplexer_1 (
    .in0(address), .in1(addr_latch_q), .out(address_latched), .sel(DMwe_latch_q));
  and and_1 (WE_latched, clk, DMwe_latch_q);
  not not_1 (OE_latched, WE_latched);
endmodule

module RIJDecide (
  input  [15:0] instruction,
  output R,
  output I,
  output J
);

  wire decoder_1_out0, decoder_1_out1, decoder_1_out2, decoder_1_out3, decoder_1_out4, decoder_1_out5,
       decoder_1_out6, decoder_1_out7, decoder_1_out8, decoder_1_out9, decoder_1_out10, decoder_1_out11,
       decoder_1_out12, decoder_1_out13, decoder_1_out14, decoder_1_out15;

  Decoder #(.select(4)) decoder_1 (
    .out0(decoder_1_out0), .out1(decoder_1_out1), .out2(decoder_1_out2), .out3(decoder_1_out3),
    .out4(decoder_1_out4), .out5(decoder_1_out5), .out6(decoder_1_out6), .out7(decoder_1_out7),
    .out8(decoder_1_out8), .out9(decoder_1_out9), .out10(decoder_1_out10), .out11(decoder_1_out11),
    .out12(decoder_1_out12), .out13(decoder_1_out13), .out14(decoder_1_out14), .out15(decoder_1_out15),
    .sel(instruction[15:12]));  // open: en
  or or_1 (R, decoder_1_out0, decoder_1_out2, decoder_1_out3, decoder_1_out4, decoder_1_out5, decoder_1_out6, decoder_1_out12);
  or or_2 (J, decoder_1_out11, decoder_1_out13);
  or or_3 (I, decoder_1_out1, decoder_1_out7, decoder_1_out8, decoder_1_out9, decoder_1_out10, decoder_1_out14, decoder_1_out15);
endmodule
