// Logisim project circuit1a.circ as structural Verilog: 1 circuit, main circuit circuit1a
module circuit1a (
  input  A,
  input  B,
  input  C,
  output result
);

  wire a_t, and_1_out, and_2_out, and_3_out, and_4_out, and_5_out, b_t, c_t, or_1_out;

  not not_1 (a_t, A);
  not not_2 (b_t, B);
  not not_3 (c_t, C);
  and and_1 (and_1_out, A, B);
  and and_2 (and_2_out, a_t, b_t);
  or or_1 (or_1_out, and_1_out, and_2_out);
  and and_3 (and_3_out, c_t, or_1_out);
  and and_4 (and_4_out, a_t, b_t, C);
  and and_5 (and_5_out, C, B);
  or or_2 (result, and_3_out, and_4_out, and_5_out);
endmodule
