// Logisim project my_adder.circ as structural Verilog: 3 circuits, main circuit main
module main (
  input  sub,
  input  [15:0] A,
  input  [15:0] B,
  output [15:0] result,
  output ovf
);

  BitAdder16 bitadder16_1 (.sub(sub), .A(A), .B(B), .result(result), .ovf(ovf));  // open: out_6
endmodule

module OneBitAdder (
  input  A,
  input  B,
  input  Cin,
  output result,
  output Cout
);

  wire and_1_out, and_2_out, xor_1_out;

  xor xor_1 (xor_1_out, A, B);
  and and_1 (and_1_out, A, B);
  xor xor_2 (result, Cin, xor_1_out);
  and and_2 (and_2_out, xor_1_out, Cin);
  or or_1 (Cout, and_2_out, and_1_out);

  // Other names for the same wires on the sheet: C = Cin
endmodule

module BitAdder16 (
  input  sub,
  input  [15:0] A,
  input  [15:0] B,
  output [15:0] result,
  output ovf,
  output out_6
);

  wire and_1_out, B1, B2, B3, B4, B5, B6, B7, B8, B9, B10, B11, B12, B13, B14, B15, B16, Cout1, Cout2, Cout3,
       Cout4, Cout5, Cout6, Cout7, Cout8, Cout9, Cout10, Cout11, Cout12, Cout13, Cout14, Cout15,
       onebitadder_16_cout, undriven, xor_17_out;

  xor xor_1 (B1, sub, B[0]);
  xor xor_2 (B2, sub, B[1]);
  xor xor_3 (B3, sub, B[2]);
  xor xor_4 (B4, sub, B[3]);
  xor xor_5 (B5, sub, B[4]);
  xor xor_6 (B6, sub, B[5]);
  xor xor_7 (B7, sub, B[6]);
  xor xor_8 (B8, sub, B[7]);
  xor xor_9 (B9, sub, B[8]);
  xor xor_10 (B10, sub, B[9]);
  xor xor_11 (B11, sub, B[10]);
  xor xor_12 (B12, sub, B[11]);
  xor xor_13 (B13, sub, B[12]);
  xor xor_14 (B14, sub, B[13]);
  xor xor_15 (B15, sub, B[14]);
  xor xor_16 (B16, sub, B[15]);
  buf xor_17 (xor_17_out, undriven);  // XOR_Gate
  OneBitAdder onebitadder_1 (.A(A[0]), .B(B1), .Cin(sub), .result(result[0]), .Cout(Cout1));
  OneBitAdder onebitadder_2 (.A(A[1]), .B(B2), .Cin(Cout1), .result(result[1]), .Cout(Cout2));
  OneBitAdder onebitadder_3 (.A(A[2]), .B(B3), .Cin(Cout2), .result(result[2]), .Cout(Cout3));
  OneBitAdder onebitadder_4 (.A(A[3]), .B(B4), .Cin(Cout3), .result(result[3]), .Cout(Cout4));
  OneBitAdder onebitadder_5 (.A(A[4]), .B(B5), .Cin(Cout4), .result(result[4]), .Cout(Cout5));
  OneBitAdder onebitadder_6 (.A(A[5]), .B(B6), .Cin(Cout5), .result(result[5]), .Cout(Cout6));
  OneBitAdder onebitadder_7 (.A(A[6]), .B(B7), .Cin(Cout6), .result(result[6]), .Cout(Cout7));
  OneBitAdder onebitadder_8 (.A(A[7]), .B(B8), .Cin(Cout7), .result(result[7]), .Cout(Cout8));
  OneBitAdder onebitadder_9 (.A(A[8]), .B(B9), .Cin(Cout8), .result(result[8]), .Cout(Cout9));
  OneBitAdder onebitadder_10 (.A(A[9]), .B(B10), .Cin(Cout9), .result(result[9]), .Cout(Cout10));
  OneBitAdder onebitadder_11 (.A(A[10]), .B(B11), .Cin(Cout10), .result(result[10]), .Cout(Cout11));
  OneBitAdder onebitadder_12 (.A(A[11]), .B(B12), .Cin(Cout11), .result(result[11]), .Cout(Cout12));
  OneBitAdder onebitadder_13 (.A(A[12]), .B(B13), .Cin(Cout12), .result(result[12]), .Cout(Cout13));
  OneBitAdder onebitadder_14 (.A(A[13]), .B(B14), .Cin(Cout13), .result(result[13]), .Cout(Cout14));
  OneBitAdder onebitadder_15 (.A(A[14]), .B(B15), .Cin(Cout14), .result(result[14]), .Cout(Cout15));
  OneBitAdder onebitadder_16 (.A(A[15]), .B(B16), .Cin(Cout15), .result(result[15]), .Cout(onebitadder_16_cout));
  and and_1 (and_1_out, xor_17_out, sub);
  xor xor_18 (ovf, onebitadder_16_cout, Cout15);
  or or_1 (out_6, undriven, and_1_out);

  // Other names for the same wires on the sheet: A1 = A[0]; A2 = A[1]; A3 = A[2]; A4 = A[3]; A5 = A[4]; A6 = A[5];
  //   A7 = A[6]; A8 = A[7]; A9 = A[8]; A10 = A[9]; A11 = A[10]; A12 = A[11]; A13 = A[12]; A14 = A[13]; A15 = A[14];
  //   A16 = A[15]; b1_t = B[0]; b2_t = B[1]; b3_t = B[2]; b4_t = B[3]; b5_t = B[4]; b6_t = B[5]; b7_t = B[6];
  //   b8_t = B[7]; b9_t = B[8]; b10_t = B[9]; b11_t = B[10]; b12_t = B[11]; b13_t = B[12]; b14_t = B[13];
  //   b15_t = B[14]; b16_t = B[15]
endmodule
